# Fritzing sketch chaveiro (saved by Fritzing 1.0.8)

parts:
  Bateria_18650_3_7_V = Bateria de lítio 18650 3,7 V (com suporte)
  D1_(1N4001) = Rectifier Diode [package="300 mil [THT]"]
  ESP-01S = ESP-01S (ESP8266)

nets:
  N1: Bateria_18650_3_7_V.+, D1_(1N4001).anode
  N2: Bateria_18650_3_7_V.-, ESP-01S.GND
  N3: D1_(1N4001).cathode, ESP-01S.3V3

custom parts:
  Bateria de lítio 18650 3,7 V (com suporte): Célula de íon-lítio 18650, 3,7 V nominal (4,2 V carregada), em suporte com fios. Peça criada para o projeto AquiIoT.
  ESP-01S (ESP8266): Módulo ESP-01S com ESP8266EX, 1 MB de flash e antena na placa. Pinos 2x4 de 0,1". O ESP-01S já traz pull-ups em EN e RST. Peça criada para o projeto AquiIoT.
