# Fritzing sketch esp32_setor (saved by Fritzing 1.0.8)
breadboards: 1

parts:
  ESP32 = ESP32 DevKit V1 (DOIT, 30 pinos)
  DHT11 = DHT11 (4 pinos)
  Microfone = Módulo sensor de som KY-037
  Buzzer = Buzzer ativo 12 mm (2 pinos)
  LDR = Photocell (LDR) [package=THT]
  R1 = Resistor [resistance=10kΩ package=THT]
  R2 = Resistor [resistance=10kΩ package=THT]

nets:
  N1: ESP32.GPIO34, LDR.pin_1, R1.Pin_0
  N2: ESP32.GPIO35, Microfone.AO
  N3: ESP32.GPIO32, DHT11.DATA, R2.Pin_1
  N4: ESP32.GPIO25, Buzzer.+
  GND: ESP32.GND, DHT11.GND, Microfone.G, Buzzer.-, R1.Pin_1
  3V3: ESP32.3V3, DHT11.VCC, Microfone.+, LDR.pin_0, R2.Pin_0

custom parts:
  ESP32 DevKit V1 (DOIT, 30 pinos): Placa ESP32 DevKit V1 (DOIT) de 30 pinos, módulo ESP-WROOM-32, USB micro e regulador 3,3 V. Pinagem conferida com a serigrafia da placa. Peça criada para o projeto AquiIoT.
  DHT11 (4 pinos): Sensor DHT11 de temperatura e umidade, componente avulso de 4 pinos (passo 0,1"). O pino de dados precisa de resistor de pull-up (10 kΩ para VCC). Peça criada para o projeto AquiIoT.
  Módulo sensor de som KY-037: Módulo KY-037 (sensibilidade ao som): microfone de eletreto grande, comparador LM393 e trimpot. AO = sinal analógico, DO = digital. Peça criada para o projeto AquiIoT.
  Buzzer ativo 12 mm (2 pinos): Buzzer ativo de 12 mm com oscilador interno: soa com nível alto no pino +. Pinos a 0,3" (7,6 mm). Peça criada para o projeto AquiIoT.
